# Fritzing sketch circuit (saved by Fritzing 0.8.4b)
breadboards: 1

parts:
  IC1 = IC, DIP package, 8 pins [chip_label=NE555]
  IC2 = IC, DIP package, 16 pins [chip_label=4017]
  C1 = Ceramic Capacitor [capacitance=1µF package="100 mil [THT, multilayer]"]
  C2 = Ceramic Capacitor [capacitance=100nF package="100 mil [THT, multilayer]"]
  R1 = Resistor [tolerance=±5% resistance=47k package=THT]
  R2 = Resistor [tolerance=±5% resistance=1k package=THT]
  P1 = Rotary Potentiometer (Small) [maximum_resistance=1mΩ package=THT]
  LED1 = LED - 5mm [color="Red (633nm)" package="5 mm [THT]"]
  LED2 = LED - 5mm [color="Red (633nm)" package="5 mm [THT]"]
  LED3 = LED - 5mm [color="Red (633nm)" package="5 mm [THT]"]
  LED4 = LED - 5mm [color="Red (633nm)" package="5 mm [THT]"]
  LED5 = LED - 5mm [color="Red (633nm)" package="5 mm [THT]"]
  LED6 = LED - 5mm [color="Red (633nm)" package="5 mm [THT]"]
  LED7 = LED - 5mm [color="Red (633nm)" package="5 mm [THT]"]
  LED8 = LED - 5mm [color="Red (633nm)" package="5 mm [THT]"]
  P2_(8x) = Rotary Potentiometer (Small) [maximum_resistance=100kΩ package=THT]
  R3_(8x) = Resistor [tolerance=±5% resistance=470 package=THT]
  R5 = Resistor [tolerance=±5% resistance=10k package=THT]
  R6 = Resistor [tolerance=±5% resistance=10k package=THT]
  R7 = Resistor [tolerance=±5% resistance=10k package=THT]
  R8 = Resistor [tolerance=±5% resistance=10k package=THT]
  R9 = Resistor [tolerance=±5% resistance=10k package=THT]
  R10 = Resistor [tolerance=±5% resistance=10k package=THT]
  R11 = Resistor [tolerance=±5% resistance=10k package=THT]
  R12 = Rotary Potentiometer (Small) [maximum_resistance=100kΩ package=THT]
  R13 = Rotary Potentiometer (Small) [maximum_resistance=100kΩ package=THT]
  R14 = Rotary Potentiometer (Small) [maximum_resistance=100kΩ package=THT]
  R15 = Rotary Potentiometer (Small) [maximum_resistance=100kΩ package=THT]
  R16 = Rotary Potentiometer (Small) [maximum_resistance=100kΩ package=THT]
  R17 = Rotary Potentiometer (Small) [maximum_resistance=100kΩ package=THT]
  R18 = Rotary Potentiometer (Small) [maximum_resistance=100kΩ package=THT]
  D1_(8x) = Rectifier Diode [part_number=1N4007 package="300 mil [THT]"]
  D2 = Rectifier Diode [part_number=1N4001 package="300 mil [THT]"]
  D3 = Rectifier Diode [part_number=1N4001 package="300 mil [THT]"]
  D4 = Rectifier Diode [part_number=1N4001 package="300 mil [THT]"]
  D5 = Rectifier Diode [part_number=1N4001 package="300 mil [THT]"]
  D6 = Rectifier Diode [part_number=1N4001 package="300 mil [THT]"]
  D7 = Rectifier Diode [part_number=1N4001 package="300 mil [THT]"]
  D8 = Rectifier Diode [part_number=1N4001 package="300 mil [THT]"]
  Q1 = NPN-Transistor [part_number=C547B package="TO92 [THT]"]
  R5_2 = Resistor [tolerance=±5% resistance=22k package=THT]
  R6_2 = Resistor [tolerance=±5% resistance=27k package=THT]
  R4 = Resistor [tolerance=±5% resistance=22k package=THT]
  R7_2 = Resistor [tolerance=±20% resistance=100k package=THT]

nets:
  GND: IC1.pin1, IC2.pin8, IC2.pin13, C1.0, C2.0, LED1.cathode, LED2.cathode, LED3.cathode, LED4.cathode, LED5.cathode, LED6.cathode, LED7.cathode, LED8.cathode, P2_(8x).leg1, R12.leg1, R13.leg1, R14.leg1, R15.leg1, R16.leg1, R17.leg1, R18.leg1, R6_2.Pin_1, R7_2.Pin_1
  N1: IC1.pin2, IC1.pin6, C1.1, R1.Pin_1
  N2: IC1.pin3, IC2.pin14, P1.leg1, P1.wiper, R4.Pin_0, R7_2.Pin_0
  9V: IC1.pin4, IC1.pin8, IC2.pin16, C2.1, R2.Pin_0, Q1.C
  N3: IC1.pin7, R2.Pin_1
  N4: IC2.pin1, R6.Pin_0, R16.leg2
  N5: IC2.pin2, R10.Pin_0, R12.leg2
  N6: IC2.pin3, P2_(8x).leg2, R9.Pin_0
  N7: IC2.pin4, R11.Pin_0, R13.leg2
  N8: IC2.pin5, R5.Pin_0, R18.leg2
  N9: IC2.pin6, R3_(8x).Pin_0, R17.leg2
  N10: IC2.pin7, R8.Pin_0, R15.leg2
  N11: IC2.pin9, IC2.pin15
  N12: IC2.pin10, R7.Pin_0, R14.leg2
  N13: R1.Pin_0, P1.leg2
  N14: LED1.anode, R9.Pin_1
  N15: LED2.anode, R10.Pin_1
  N16: LED3.anode, R11.Pin_1
  N17: LED4.anode, R8.Pin_1
  N18: LED5.anode, R6.Pin_1
  N19: LED6.anode, R5.Pin_1
  N20: LED7.anode, R7.Pin_1
  N21: LED8.anode, R3_(8x).Pin_1
  N22: P2_(8x).wiper, D1_(8x).anode
  N23: R12.wiper, D2.anode
  N24: R13.wiper, D3.anode
  N25: R14.wiper, D6.anode
  N26: R15.wiper, D4.anode
  N27: R16.wiper, D7.anode
  N28: R17.wiper, D8.anode
  N29: R18.wiper, D5.anode
  CV Output: D1_(8x).cathode, D2.cathode, D3.cathode, D4.cathode, D5.cathode, D6.cathode, D7.cathode, D8.cathode
  N30: Q1.E, R5_2.Pin_0
  N31: Q1.B, R4.Pin_1
  Gate Output: R5_2.Pin_1, R6_2.Pin_0
